# Fritzing sketch TX (saved by Fritzing 0.9.3b)

parts:
  nRF24L01_PA1 = nRF24L01 power adapter [package="DIP (Dual Inline) [THT]"]
  Часть2 = Arduino Nano (Rev3.0)
  KEYPAD1 = Membrane Matrix Keypad  # not connected
  Lithium_battery_charger1 = Lithium battery charger [package="DIP (Dual Inline) [THT]"]
  18650_holder1 = 18650 holder [package="DIP (Dual Inline) [THT]"]
  IC1 = DC-DC 5V step-up [chip_label="DC-DC 5V step-up" package="DIP (Dual Inline) [THT]"]
  U1 = SWITCH_SPDT [package=kps-1290]
  LED1 = smd LED [color="Red (633nm)" package="0603 [SMD]"]
  LED2 = smd LED [color="Green (555nm)" package="0603 [SMD]"]
  R1 = Resistor [tolerance=±5% resistance=220 package="2512 [SMD]"]
  R2 = Resistor [tolerance=±5% resistance=220 package="2512 [SMD]"]

nets:
  GND: nRF24L01_PA1.GND, Часть2.GND, IC1.GND, LED2.cathode
  5V: nRF24L01_PA1.VCC, Часть2.5V, IC1.5V
  N1: nRF24L01_PA1.CE, Часть2.D9
  N2: nRF24L01_PA1.CSN, Часть2.D10
  N3: nRF24L01_PA1.SCK, Часть2.D13/SCK
  N4: nRF24L01_PA1.MO, Часть2.D11/MOSI
  N5: nRF24L01_PA1.MI, Часть2.D12/MISO
  N6: Lithium_battery_charger1.OUT+, IC1.IN+
  N7: Lithium_battery_charger1.OUT-, U1.O
  N8: Lithium_battery_charger1.Battery+, 18650_holder1.holder_+
  N9: Lithium_battery_charger1.Battery-, 18650_holder1.holder_-
  N10: IC1.IN-, U1.P
  N11: LED1.anode, R2.Pin_1
  N12: LED2.anode, R1.Pin_1

custom parts:
  nRF24L01 power adapter: Адаптер для питания nRF
  Membrane Matrix Keypad: Membrane Matrix 3x4 Keypad
  Lithium battery charger: USB зарядник для литиевых аккумуляторов + защита от КЗ и переразряда
  18650 holder: Акум формата 18650 в холдере
  DC-DC 5V step-up: Повышающий модуль постоянного напряжения
